# Fritzing sketch Stress Jacket (saved by Fritzing 0.9.3b)
circuit board: 10.7836cm x 6.63368cm
breadboards: 4

parts:
  DHT1 = DHT11 Humitidy and Temperature Sensor
  T1 = LM35 Temperature Sensor [package="TO92 [THT]"]
  T2 = LM35 Temperature Sensor [package="TO92 [THT]"]
  Grove1 = Grove Temperature Sensor
  J1 = Piezo Speaker
  J2 = Piezo Speaker
  SEN1 = Pulse Sensor [package=SIP]
  SEN2 = Pulse Sensor [package=SIP]
  Part1 = Arduino Uno (Rev3) - ICSP

nets:
  VCC: DHT1.VDD, T1.+Vs, T2.+Vs, Grove1.VCC, SEN1.Vcc, SEN2.Vcc
  N1: DHT1.DATA, Part1.A2
  GND: DHT1.GND, T1.GND, T2.GND, Grove1.GND, J1.pin1, J2.pin1, SEN1.GND, SEN2.GND, Part1.GND
  N2: T1.Vout, Part1.A0
  N3: T2.Vout, Part1.A1
  N4: Grove1.SIG, Part1.A4/SDA
  N5: J1.pin2, Part1.D9_PWM
  N6: J2.pin2, Part1.ICSP_MOSI, Part1.D11_PWM/MOSI
  N7: SEN1.Signal, Part1.A3
  N8: SEN2.Signal, Part1.A5/SCL

custom parts:
  DHT11 Humitidy and Temperature Sensor: DHT11 Humidity and Temperature Sensor
  Pulse Sensor: Pulse Sensor Optical Heart Rate Monitor for Arduino and other microcontrollers
